# Fritzing sketch sensorHat03-1 (saved by Fritzing 0.9.9b)
circuit board: 6.43246cm x 3.40399cm
breadboards: 1

parts:
  LED2 = LED - 3mm [color="Red (633nm)" current=0.030 package="3 mm [THT]"]
  iRsensor = tl1838 [package=THT]
  S1 = Momentary Switch [package=ksa_sealed_tac_switch]
  SR04 = HC-SR04 [chip_label=IC package="SIP (Single Inline) [THT]"]
  S2 = Momentary Switch [package=ksa_sealed_tac_switch]
  LED1 = LED - 3mm [color="Red (633nm)" current=0.030 package="3 mm [THT]"]
  Raspberry_Pi1 = Raspberry Pi 2
  C1 = Electrolytic Capacitor [capacitance=1µF package="100 mil [THT, electrolytic]"]
  cds = PHOTOCELL [package=photocell]
  Q1 = NPN-Transistor [package="TO92 [THT]"]
  R3 = Resistor [tolerance=±5% resistance=22 power=0.25 package=THT]
  R5 = 1kΩ Resistor [package=THT]
  iR-LED = LED - 3mm [color="Infrared (940nm)" current=0.030 package="3 mm [THT]"]
  R8 = Resistor [tolerance=±5% resistance=470 power=0.25 package=THT]
  R7 = Resistor [tolerance=±5% resistance=10k power=0.25 package=THT]
  S3 = Tilt Switch [package=THT]
  R1 = Resistor [tolerance=±5% resistance=10k power=0.25 package=THT]
  R1_2 = Resistor [tolerance=±5% resistance=10k power=0.25 package=THT]
  R4 = Resistor [tolerance=±5% resistance=470 power=0.25 package=THT]
  R4_2 = Resistor [tolerance=±5% resistance=470 power=0.25 package=THT]
  R2 = Resistor [tolerance=±5% resistance=4.7k power=0.25 package=THT]
  R2_2 = Resistor [tolerance=±5% resistance=4.7k power=0.25 package=THT]
  R2_3 = Resistor [tolerance=±5% resistance=4.7k power=0.25 package=THT]

nets:
  GND: LED2.cathode, iRsensor.GND, SR04.GND, LED1.cathode, Raspberry_Pi1.GND, C1.-, Q1.E, R7.Pin_0, R2_2.Pin_0, R2_3.Pin_0
  N1: LED2.anode, R4_2.Pin_1
  N2: iRsensor.OUT, Raspberry_Pi1.GPIO4
  3V3: iRsensor.VCC, S1.3, S1.4, S2.3, S2.4, Raspberry_Pi1.3v3, Raspberry_Pi1.3V3, R8.Pin_1, S3.Pin_2
  N3: S1.1, S1.2, R1.Pin_1, R2_3.Pin_1
  VCC: SR04.Vcc, Raspberry_Pi1.5V, C1.+, R3.Pin_0
  N4: SR04.Trig, Raspberry_Pi1.GPIO24
  N5: SR04.Echo, Raspberry_Pi1.GPIO23
  N6: S2.1, S2.2, R1_2.Pin_1, R2_2.Pin_1
  N7: LED1.anode, R4.Pin_1
  N8: Raspberry_Pi1.GPIO17, R4_2.Pin_0
  N9: Raspberry_Pi1.GPIO27, R4.Pin_0
  N10: Raspberry_Pi1.GPIO22, R5.Pin_0
  N11: Raspberry_Pi1.GPIO5, R1_2.Pin_0
  N12: Raspberry_Pi1.GPIO6, R1.Pin_0
  N13: Raspberry_Pi1.GPIO26, R2.Pin_0
  N14: Raspberry_Pi1.GPIO21, cds.P$1, R7.Pin_1
  N15: cds.P$2, R8.Pin_0
  N16: Q1.B, R5.Pin_1
  N17: Q1.C, iR-LED.cathode
  N18: R3.Pin_1, iR-LED.anode
  N19: S3.Pin_1, R2.Pin_1

notes:
  G
  V
  3.3v
  5v
  E
  T
  BMP180
  21
  TKJ-seisakusho  sensorHAT-v03-1
  SCL
  SDA
  C1
  AHT10
  S

custom parts:
  tl1838: The TL1838 is a miniaturized receiver for infrared remote control systems. A PIN diode and a preamplifier are assembled on a lead frame, the epoxy package acts as an IR filter. The demodulated output signal can be directly decoded by a microprocessor.
  HC-SR04: HC-SR04 ultrasound distance sensor
  1kΩ Resistor: A generic resistor (0.25W)
