# Fritzing sketch sensorHat04-ADC-03 (saved by Fritzing 0.9.9b)
circuit board: 6.46069cm x 3.54511cm
breadboards: 1

parts:
  LED2 = LED - 3mm [color="Red (633nm)" current=0.030 package="3 mm [THT]"]
  iRsensor = tl1838 [package=THT]
  S1 = Momentary Switch [package=ksa_sealed_tac_switch]
  SR04 = HC-SR04 [chip_label=IC package="SIP (Single Inline) [THT]"]
  S2 = Momentary Switch [package=ksa_sealed_tac_switch]
  LED1 = LED - 3mm [color="Red (633nm)" current=0.030 package="3 mm [THT]"]
  cds = PHOTOCELL [package=photocell]
  TR = NPN-Transistor [package="TO92 [THT]"]
  R3 = Resistor [tolerance=±5% resistance=22 power=0.25 package=THT]
  iR-LED = LED - 3mm [color="Infrared (940nm)" current=0.030 package="3 mm [THT]"]
  R8 = Resistor [tolerance=±5% resistance=470 power=0.25 package=THT]
  R7 = Resistor [tolerance=±5% resistance=10k power=0.25 package=THT]
  S3 = Tilt Switch [package=THT]
  R1 = Resistor [tolerance=±5% resistance=10k power=0.25 package=THT]
  R1_2 = Resistor [tolerance=±5% resistance=10k power=0.25 package=THT]
  R4 = Resistor [tolerance=±5% resistance=470 power=0.25 package=THT]
  R4_2 = Resistor [tolerance=±5% resistance=470 power=0.25 package=THT]
  R2 = Resistor [tolerance=±5% resistance=4.7k power=0.25 package=THT]
  R2_2 = Resistor [tolerance=±5% resistance=4.7k power=0.25 package=THT]
  R2_3 = Resistor [tolerance=±5% resistance=4.7k power=0.25 package=THT]
  MCP3002 = IC, DIP package, 8 pins [chip_label=IC]
  R5 = Resistor [tolerance=±5% resistance=470 power=0.25 package=THT]
  J1 = Raspberry Pi Header 40pin [package=THT]
  3-hole1 = 3-hole [package=1x03]
  3-hole2 = 3-hole [package=1x03]
  4-hole1 = 4-hole
  R6 = TRIMPOT [package=3386u]  # not connected

nets:
  GND: LED2.cathode, iRsensor.GND, SR04.GND, LED1.cathode, TR.E, R7.Pin_0, R2_2.Pin_0, R2_3.Pin_0, MCP3002.pin4, J1.GND, 3-hole1.3, 3-hole2.1, 4-hole1.3
  N1: LED2.anode, R4_2.Pin_1
  N2: iRsensor.OUT, J1.IO4
  VCC: iRsensor.VCC, S1.3, S1.4, S2.3, S2.4, R8.Pin_1, S3.Pin_2, MCP3002.pin8, J1.3V3, 3-hole1.2, 4-hole1.4
  N3: S1.1, S1.2, R1.Pin_1, R2_3.Pin_1
  VCC_2: SR04.Vcc, R3.Pin_0, J1.5V
  N4: SR04.Trig, J1.IO24
  N5: SR04.Echo, J1.IO23
  N6: S2.1, S2.2, R1_2.Pin_1, R2_2.Pin_1
  N7: LED1.anode, R4.Pin_1
  N8: cds.P$1, R7.Pin_1, MCP3002.pin2, J1.IO21, 3-hole2.3
  N9: cds.P$2, R8.Pin_0
  N10: TR.B, R5.Pin_0
  N11: TR.C, iR-LED.cathode
  N12: R3.Pin_1, iR-LED.anode
  N13: S3.Pin_1, R2.Pin_1
  N14: R1.Pin_0, J1.IO6
  N15: R1_2.Pin_0, J1.IO5
  N16: R4.Pin_0, J1.IO27
  N17: R4_2.Pin_0, J1.IO17
  N18: R2.Pin_0, J1.IO26
  N19: MCP3002.pin1, J1.IO8
  N20: MCP3002.pin3, 3-hole2.2
  N21: MCP3002.pin5, J1.IO10
  N22: MCP3002.pin6, J1.IO9
  N23: MCP3002.pin7, J1.IO11
  N24: R5.Pin_1, J1.IO22
  N25: J1.GPIO2, 4-hole1.1
  N26: J1.IO3, 4-hole1.2
  N27: J1.IO25, 3-hole1.1

notes:
  G
  V
  5v
  E
  T
  BMP180
  sensorHAT-v04-3
  SDA
  SCL
  1
  AHT10
  S
  TKJ-seisakusho
  0
  analog
  C
  potention
  meter

custom parts:
  tl1838: The TL1838 is a miniaturized receiver for infrared remote control systems. A PIN diode and a preamplifier are assembled on a lead frame, the epoxy package acts as an IR filter. The demodulated output signal can be directly decoded by a microprocessor.
  HC-SR04: HC-SR04 ultrasound distance sensor
  Raspberry Pi Header 40pin: Raspberry Pi 40 pin header - for creating your own shields. (Mar 2020, bb: make breadboard friendly (.4in pin spacing) and add labels. Schematic add labels. PCB make oblong pins to allow routing traces between the pins.)
  3-hole: Half-wheatstone bridge Load Cell
  4-hole: Digital relative humidity & temperature sensor RHT03
  TRIMPOT: Various small potentiometers for set-and-forget applications
